// Digital circuit a.dig as structural Verilog
module a (
  input  A0,
  input  A1,
  input  A2,
  input  A3,
  output a
);

  wire and_1_out, and_2_out, and_3_out;

  and and_1 (and_1_out, ~A0, ~A1, ~A3);  // And
  and and_2 (and_2_out, ~A0, A1, A3);  // And
  and and_3 (and_3_out, A0, ~A1, ~A2, A3);  // And
  or or_1 (a, and_1_out, and_2_out, and_3_out);
endmodule
