// Digital circuit complete.dig as structural Verilog
module complete (
  input  A0,
  input  A1,
  input  A2,
  input  A3
);

  wire a_1_a, b_1_b, c_1_c, d_1_d, e_1_e, f_1_f, g_1_g;

  a a_1 (.A0(A0), .A1(A1), .A2(A2), .A3(A3), .a(a_1_a));
  b b_1 (.A0(A0), .A1(A1), .A2(A2), .A3(A3), .b(b_1_b));
  c c_1 (.A0(A0), .A1(A1), .A2(A2), .A3(A3), .c(c_1_c));
  d d_1 (.A0(A0), .A1(A1), .A2(A2), .A3(A3), .d(d_1_d));
  e e_1 (.\А0 (A0), .\А1 (A1), .\А3 (A3), .e(e_1_e));
  f f_1 (.A0(A0), .A1(A1), .A2(A2), .A3(A3), .f(f_1_f));
  g g_1 (.A0(A0), .A1(A1), .A2(A2), .A3(A3), .g(g_1_g));
  Seven_Seg seven_seg_1 (.a(a_1_a), .b(b_1_b), .c(c_1_c), .d(d_1_d), .e(e_1_e), .f(f_1_f), .g(g_1_g), .dp(1'b0));
endmodule
